# Fritzing sketch Rudolph_step_3 (saved by Fritzing 0.9.3b)
breadboards: 1

parts:
  Arduino1 = Arduino Uno (Rev3)
  LED1 = LED - 3mm [color="Red (633nm)" package="3 mm [THT]"]
  R1 = Resistor [tolerance=±5% resistance=220 package=THT]  # not connected
  J1 = Piezo Speaker

nets:
  N1: Arduino1.D9_PWM, J1.pin2
  N2: Arduino1.GND, LED1.anode, J1.pin1

notes:
  BLINK

// code stored in the sketch: Blink.ino
/*
  Blink
  
  Schaltet eine LED im Rythmus von einer Sekunde an und aus
  
  Dieses Beispiel aus dem Fritzing Creator Kit: www.fritzing.org/creator-kit.
*/

int led = 13;                   // ganzzahlige Variable led wird deklariert

void setup() {                  // die setup()-Methode wird einmal ausgeführt
  pinMode(led, OUTPUT);     
}

void loop() {                   // die loop()-Methode wird immer wiederholt
  digitalWrite(led, HIGH);      // schaltet die LED ein 
  delay(1000);                  // hält das Programm für 1000 Millisekunden an
  digitalWrite(led, LOW);       // schaltet die LED ab
  delay(1000);                  // hält das Programm für 1000 Millisekunden an
}
