# Fritzing sketch Rudolph_step_4 (saved by Fritzing 0.9.3b)
breadboards: 1

parts:
  Arduino1 = Arduino Uno (Rev3)
  LED1 = LED - 3mm [color="Red (633nm)" package="3 mm [THT]"]
  R1 = Resistor [tolerance=±5% resistance=220 package=THT]
  J1 = Piezo Speaker
  R2 = Photocell (LDR) [package=THT]
  R3 = Resistor [tolerance=±5% resistance=10k package=THT]
  S1 = Pushbutton [package="[THT]"]
  R4 = Resistor [tolerance=±5% resistance=10k package=THT]

nets:
  N1: Arduino1.A0, R2.pin_1, R3.Pin_0
  N2: Arduino1.D9_PWM, J1.pin2
  N3: Arduino1.D2, S1.Pin_3, S1.Pin_4, R4.Pin_0
  N4: Arduino1.5V, R1.Pin_0, R2.pin_0, S1.Pin_1, S1.Pin_2
  N5: Arduino1.GND, LED1.anode, J1.pin1, R3.Pin_1, R4.Pin_1

notes:
  BLINK

// code stored in the sketch: Blink.ino
/*
  Blink
  
  Schaltet eine LED im Rythmus von einer Sekunde an und aus
  
  Dieses Beispiel aus dem Fritzing Creator Kit: www.fritzing.org/creator-kit.
*/

int led = 13;                   // ganzzahlige Variable led wird deklariert

void setup() {                  // die setup()-Methode wird einmal ausgeführt
  pinMode(led, OUTPUT);     
}

void loop() {                   // die loop()-Methode wird immer wiederholt
  digitalWrite(led, HIGH);      // schaltet die LED ein 
  delay(1000);                  // hält das Programm für 1000 Millisekunden an
  digitalWrite(led, LOW);       // schaltet die LED ab
  delay(1000);                  // hält das Programm für 1000 Millisekunden an
}
